// Logisim project Logic Gates .circ as structural Verilog: 1 circuit, main circuit main
module main (
  input  in_1,
  input  in_2,
  input  in_3,
  input  in_4,
  input  in_5,
  input  in_6,
  input  in_7,
  input  in_8,
  input  in_9,
  input  in_10,
  input  in_11,
  output out_12,
  output out_13,
  output out_14,
  output out_15,
  output out_16,
  output out_17
);

  xor xor_1 (out_12, in_1, in_2);
  and and_1 (out_13, in_3, in_4);
  or or_1 (out_14, in_5, in_6);
  nor nor_1 (out_15, in_7, in_8);
  not not_1 (out_16, in_9);
  nand nand_1 (out_17, in_10, in_11);

  // Notes on the sheet:
  //   XOR - GATE
  //   AND - GATE
  //   OR - GATE 
  //   NOR - GATE 
  //   NOT - GATE
  //   NAND - GATE
endmodule
